# Fritzing sketch Untitled Sketch (saved by Fritzing 0.9.2b)

parts:
  e-radionica1 = TCS230 Color Sensor [part_number=101209]
  Part1 = Arduino Uno (Rev3)
  LED1 = LED - 5mm [color="Red (633nm)" package="5 mm [THT]"]
  R1 = Resistor [tolerance=±5% resistance=220 package="0603 [SMD]"]

nets:
  GND: e-radionica1.Gnd, Part1.GND, LED1.cathode
  N1: e-radionica1.S1, Part1.D5_PWM
  N2: e-radionica1.S0, Part1.D4
  N3: e-radionica1.S3, Part1.D7
  N4: e-radionica1.S2, Part1.D6_PWM
  N5: e-radionica1.Out, Part1.D8
  VCC: e-radionica1.Vcc, Part1.5V
  N6: Part1.D12/MISO, R1.Pin_1

custom parts:
  TCS230 Color Sensor: TCS230
