# Fritzing sketch LDR (saved by Fritzing 0.9.3b)
breadboards: 1

parts:
  Part1 = Arduino Uno (Rev3)
  R1 = Photocell (LDR) [package=THT]
  R2 = Resistor [tolerance=±5% resistance=100k package="0603 [SMD]"]
  J1 = Basic Servo

nets:
  N1: Part1.A0, R1.pin_1, R2.Pin_0
  GND: Part1.GND, R2.Pin_1, J1.gnd
  N2: Part1.D3_PWM, J1.pulse
  5V: Part1.5V, R1.pin_0, J1.vcc
